// Digital circuit hw1_2-bitmultiplier.dig as structural Verilog
module hw1_2_bitmultiplier (
  input  A1,
  input  A0,
  input  B1,
  input  B0,
  output P3,
  output P1,
  output P0,
  output P2
);

  wire and_1_out, and_2_out, and_4_out, and_5_out;

  and and_1 (and_1_out, A1, B0);
  and and_2 (and_2_out, A0, B1);
  and and_3 (P0, A0, B0);
  and and_4 (and_4_out, B1, A1);
  xor xor_1 (P1, and_1_out, and_2_out);
  and and_5 (and_5_out, and_1_out, and_2_out);
  or or_1 (P2, and_5_out, and_4_out);
  and and_6 (P3, P2, and_4_out);
endmodule
