// Digital circuit hw1_full_adder.dig as structural Verilog
module hw1_full_adder (
  input  A1,
  input  A2,
  input  A3,
  input  A0,
  input  B3,
  input  B2,
  input  B1,
  input  B0,
  input  Cin,
  output Cout,
  output S4,
  output S3,
  output S2,
  output S1
);

  wire Fa1_cout, Fa2_cout, Fa3_cout;

  _1_bitAdder Fa4 (.A(A3), .B(B3), .Cin(Fa3_cout), .Sum(S4), .Cout(Cout));
  _1_bitAdder Fa3 (.A(A2), .B(B2), .Cin(Fa2_cout), .Sum(S3), .Cout(Fa3_cout));
  _1_bitAdder Fa2 (.A(A1), .B(B1), .Cin(Fa1_cout), .Sum(S2), .Cout(Fa2_cout));
  _1_bitAdder Fa1 (.A(A0), .B(B0), .Cin(Cin), .Sum(S1), .Cout(Fa1_cout));
endmodule
